// Digital circuit decoder.dig as structural Verilog
module decoder (
  input  [15:0] rdval,
  input  [15:0] rsval,
  input  mem,
  input  [15:0] instr,
  output [1:0] rs,
  output [1:0] rd,
  output [15:0] L,
  output [15:0] R,
  output [4:0] op,
  output rs_valid,
  output rd_valid,
  output [2:0] cond
);

  wire imm5_valid, imm6_valid, imm8_valid, imm12_valid, imm_valid, off5_valid;
  wire [3:2] multiplexer_7_out, multiplexer_8_out;
  wire [15:0] bitextender_1_out, bitextender_2_out, bitextender_3_out, bitextender_4_out, multiplexer_1_out,
       multiplexer_2_out, multiplexer_3_out, multiplexer_4_out, multiplexer_5_out, multiplexer_6_out,
       or_1_out;

  BitExtender #(.inputBits(5)) bitextender_1 (.in(instr[11:7]), .out(bitextender_1_out));
  BitExtender #(.inputBits(6)) bitextender_2 (.in(instr[11:6]), .out(bitextender_2_out));
  BitExtender bitextender_3 (.in(instr[11:4]), .out(bitextender_3_out));
  BitExtender #(.inputBits(12)) bitextender_4 (.in(instr[15:4]), .out(bitextender_4_out));
  Multiplexer #(.Bits(16)) multiplexer_1 (
    .sel(off5_valid), .in_0({16{1'b0}}), .in_1({{11{1'b0}}, instr[7:3]}), .out(multiplexer_1_out));
  Multiplexer #(.Bits(16)) multiplexer_2 (
    .sel(imm5_valid), .in_0({16{1'b0}}), .in_1(bitextender_1_out), .out(multiplexer_2_out));
  Multiplexer #(.Bits(16)) multiplexer_3 (
    .sel(imm6_valid), .in_0({16{1'b0}}), .in_1(bitextender_2_out), .out(multiplexer_3_out));
  Multiplexer #(.Bits(16)) multiplexer_4 (
    .sel(imm8_valid), .in_0({16{1'b0}}), .in_1(bitextender_3_out), .out(multiplexer_4_out));
  Multiplexer #(.Bits(16)) multiplexer_5 (
    .sel(imm12_valid), .in_0({16{1'b0}}), .in_1(bitextender_4_out), .out(multiplexer_5_out));
  instrdecoder instrdecoder_1 (
    .fmt(instr[2:0]), .op0(instr[7:3]), .op(op), .rd_valid(rd_valid), .rs_valid(rs_valid),
    .off5_valid(off5_valid), .imm5_valid(imm5_valid), .imm6_valid(imm6_valid), .imm8_valid(imm8_valid),
    .imm12_valid(imm12_valid), .imm_valid(imm_valid));
  assign or_1_out = multiplexer_1_out | multiplexer_2_out | multiplexer_3_out | multiplexer_4_out | multiplexer_5_out;  // Or or_1, 16 bits wide
  Multiplexer #(.Bits(16)) multiplexer_6 (.sel(rs_valid), .in_0({16{1'b0}}), .in_1(rsval), .out(multiplexer_6_out));
  Multiplexer #(.Bits(4)) multiplexer_7 (
    .sel(rs_valid), .in_0(4'b0000), .in_1(instr[11:8]), .out({multiplexer_7_out, rs}));
  Multiplexer #(.Bits(4)) multiplexer_8 (
    .sel(rd_valid), .in_0(4'b0000), .in_1(instr[15:12]), .out({multiplexer_8_out, rd}));
  Multiplexer #(.Bits(16)) multiplexer_9 (.sel(imm_valid), .in_0(multiplexer_6_out), .in_1(or_1_out), .out(R));
  Multiplexer #(.Bits(16)) multiplexer_10 (.sel(mem), .in_0(rdval), .in_1(or_1_out), .out(L));

  assign cond = instr[6:4];

  // Other names for the same wires on the sheet: fmt[2:0] = instr[2:0]; op0[4:0] = instr[7:3];
  //   rs_i[3:0] = instr[11:8]; rd_i[3:0] = instr[15:12]
endmodule

/* Test case load store (ls):
instr                          rsval  rs  rdval  rd  L  R  op
0b0000000000000100             5      0   0      0   0  0  0   
0b0000000000000101             5      0   0      0   0  0  1   
0b0000000000000111             5      0   0      0   0  0  3   
0b0000000000011101             5      0   9      3   9  0  1   
0b0011100100011101             5      2   9      3   9  7  1   
*/

/* Test case rr:
instr                          rsval  rs  rdval  rd  L  R  op
0b0000000000000010             5      0   2      0   2  5  0   	
0b1111100000011010             5      0   2      3   2  5  31  
0b1000000110011010             5      3   2      3   2  5  16   
*/

/* Test case i11:
instr                          rsval  rs  rdval  rd  L   R      op       sys 
0b0000000000000001             5      0   2      0   2   0      0b00100   0
0b0000000000011001             5      0   2      0   2   0      0b00111   0
0b0100000000111001             5      0   2      0   2   0x201  0b00111   0
0b1111111110111001             5      0   2      0   2   0xFFFD 0b00111   0

0b0000000000000000             5      0   2      0   2   0      8         1
0b0000000000011000             5      0   2      0   2   0      8         1
0b0100000000111000             5      0   2      0   2   0x201  8         1
0b1111111110111000             5      0   2      0   2   0xFFFD 8         1
*/

/* Test case ri:
instr                          rsval  rs  rdval  rd  L   R      op        
0b0000000000000011             5      0   2      0   2  0       0b10000   
0b0000000100011011             5      0   2      3   2  0       0b10010   
0b1000100100011011             5      0   2      3   2  0xfff1  0b10010   
0b0100100100011011             5      0   2      3   2  9       0b10010   
*/
