// Digital circuit instrdecoder.dig as structural Verilog
module instrdecoder (
  input  [2:0] fmt,
  input  [4:0] op0,
  output [4:0] op,
  output rd_valid,
  output rs_valid,
  output off5_valid,
  output imm5_valid,
  output imm6_valid,
  output imm8_valid,
  output imm12_valid,
  output imm_valid
);

  wire decoder_1_out_6, decoder_1_out_7, rr, rrc;

  Decoder #(.Selector_Bits(3)) decoder_1 (
    .sel(fmt), .out_0(rr), .out_1(imm6_valid), .out_2(rrc), .out_3(imm5_valid), .out_4(imm8_valid),
    .out_5(imm12_valid), .out_6(decoder_1_out_6), .out_7(decoder_1_out_7));
  or or_1 (off5_valid, decoder_1_out_6, decoder_1_out_7);
  or or_2 (rs_valid, off5_valid, rrc, rr);
  not not_1 (rd_valid, imm12_valid);
  nor nor_1 (imm_valid, rr, rrc, off5_valid);
  Multiplexer #(.Selector_Bits(3), .Bits(5)) multiplexer_1 (
    .sel(fmt), .in_0(op0), .in_1({2'b10, op0[2:0]}), .in_2({4'b1100, op0[0]}), .in_3({4'b1100, op0[0]}),
    .in_4({4'b1101, op0[0]}), .in_5({4'b1110, op0[0]}), .in_6({4'b1111, fmt[0]}), .in_7({4'b1111, fmt[0]}),
    .out(op));

  // Other names for the same wires on the sheet: i12 = imm12_valid; ls = off5_valid; ri6 = imm6_valid;
  //   ri8 = imm8_valid; ric = imm5_valid
endmodule
