// Digital circuit Execute.dig as structural Verilog
module Execute (
  input  [15:0] L,
  input  [15:0] R,
  input  [2:0] op,
  input  [2:0] cond,
  output [15:0] result,
  output t_in
);

  wire eq, eq_eq;
  wire [15:0] add_1_s;

  Decoder #(.Selector_Bits(3)) decoder_1 (
    .sel(op), .out_4(eq));  // open: out_0, out_1, out_2, out_3, out_5, out_6, out_7
  Add #(.Bits(16)) add_1 (.a(L), .b(R), .c_i(1'b0), .s(add_1_s));  // open: c_o
  Comparator #(.Bits(16)) u_eq (.a(R), .b(L), .eq(eq_eq));  // open: gt, lt
  Multiplexer #(.Selector_Bits(3), .Bits(16)) multiplexer_1 (
    .sel(op), .in_0(add_1_s), .in_1({16{1'b0}}), .in_2({16{1'b0}}), .in_3({16{1'b0}}), .in_4(L), .in_5(L),
    .in_6(R), .in_7(L), .out(result));
  and and_1 (t_in, eq, eq_eq);
endmodule
