// Digital circuit brindha32.dig as structural Verilog
module brindha32 (
  input  clock,
  input  step,
  input  run,
  input  [15:0] D_prog,
  input  [15:0] D_in,
  output [15:0] R0,
  output [15:0] R1,
  output [15:0] R2,
  output [7:0] PC,
  output [15:0] R3,
  output halt,
  output error,
  output T_0,
  output rd_valid,
  output rs_valid,
  output [4:0] op,
  output [2:0] cond,
  output stall,
  output [15:0] L,
  output [15:0] R,
  output [1:0] rd,
  output [1:0] rs,
  output jump,
  output [7:0] A_prog,
  output clock_m,
  output w_en,
  output [15:0] D_out,
  output [13:0] A_data
);

  wire control_1_en_fetch, control_1_mem, en, execute_1_t_in;
  wire [1:0] control_1_memop;
  wire [2:0] control_1_aluop;
  wire [15:0] execute_1_result, fetch_1_instr_o, memaccess_1_wrval, regfile_1_rdval, regfile_1_rsval;

  not not_1 (clock_m, clock);
  Fetch fetch_1 (
    .instr_i(D_prog), .clock(clock), .en(control_1_en_fetch), .jump(jump), .value(R), .pc(A_prog),
    .instr_o(fetch_1_instr_o));
  decoder decoder_1 (
    .rdval(regfile_1_rdval), .rsval(regfile_1_rsval), .mem(control_1_mem), .instr(fetch_1_instr_o), .rs(rs),
    .rd(rd), .L(L), .R(R), .op(op), .rs_valid(rs_valid), .rd_valid(rd_valid), .cond(cond));
  clockctrl clockctrl_1 (.clock(clock), .step(step), .run(run), .stall(stall));
  control control_1 (
    .op(op), .stall(stall), .clock(clock), .t_in(execute_1_t_in), .aluop(control_1_aluop), .t(T_0),
    .halt(halt), .error(error), .en_wright(en), .mem(control_1_mem), .memop(control_1_memop),
    .en_fetch(control_1_en_fetch), .jump(jump));
  Execute execute_1 (.L(L), .R(R), .op(control_1_aluop), .cond(cond), .result(execute_1_result), .t_in(execute_1_t_in));
  memaccess memaccess_1 (
    .result(execute_1_result), .rdval(regfile_1_rdval), .mem(control_1_mem), .memop(control_1_memop),
    .D(D_in), .en(en), .wrval(memaccess_1_wrval), .A(A_data), .str(w_en), .D_in(D_out));
  regfile regfile_1 (
    .rs(rs), .rd(rd), .result(memaccess_1_wrval), .clock(clock), .en(en), .rdval(regfile_1_rdval),
    .rsval(regfile_1_rsval), .R0(R0), .R1(R1), .R2(R2), .R3(R3));

  assign PC = A_prog;

  // Other names for the same wires on the sheet: A_datat[13:0] = A_data; C = clock; cond_t[2:0] = cond;
  //   D_int[15:0] = D_in; D_outt[15:0] = D_out; D_progt[15:0] = D_prog; error_t = error; halt_t = halt; jump_t = jump;
  //   L_t[15:0] = L; op_t[4:0] = op; A_progt[7:0] = A_prog; PC_t[7:0] = A_prog; R_t[15:0] = R; rd_t[1:0] = rd;
  //   rdvalid_t = rd_valid; rs_t[1:0] = rs; rsvalid_t = rs_valid; stall_t = stall; T_t = T_0; W_ent = w_en

  // Notes on the sheet:
  //   clock: Hz: 10
endmodule
