// Digital circuit control.dig as structural Verilog
module control (
  input  [4:0] op,
  input  stall,
  input  clock,
  input  t_in,
  output [2:0] aluop,
  output t,
  output halt,
  output error,
  output en_wright,
  output mem,
  output [1:0] memop,
  output en_fetch,
  output jump
);

  wire and_1_out, and_4_out, and_5_out, not_2_out, xor_1_out;
  wire [0:0] and_2_out;

  and and_1 (and_1_out, op[0], ~op[1], 1'b0, en_fetch);  // And
  and and_2 (and_2_out[0], ~op[3], op[4], ~1'b0);  // And
  and and_3 (mem, ~1'b0, ~op[4], ~op[3], ~op[2]);  // And
  not not_1 (en_fetch, stall);
  and and_4 (and_4_out, op[2], ~op[3], ~op[4]);  // And
  Register u_t (.D(t_in), .C(clock), .en(en_fetch), .Q(t));
  Multiplexer #(.Selector_Bits(2), .Bits(3)) multiplexer_1 (
    .sel({mem, and_2_out[0]}), .in_0(3'b111), .in_1(op[2:0]), .in_2(3'b000), .in_3(3'b000), .out(aluop));
  and and_5 (and_5_out, op[1], op[2], ~op[3], ~op[4]);  // And
  xor xor_1 (xor_1_out, op[0], t);
  not not_2 (not_2_out, t);
  Multiplexer #(.Bits(2)) multiplexer_2 (.sel(mem), .in_0(2'b00), .in_1(op[1:0]), .out(memop));
  Multiplexer multiplexer_3 (.sel(and_5_out), .in_0(and_4_out), .in_1(xor_1_out), .out(jump));
  and and_6 (halt, t, and_1_out);
  and and_7 (error, and_1_out, not_2_out);

  assign en_wright = en_fetch;

  // Other names for the same wires on the sheet: en_halt = en_fetch; en_t = en_fetch

  // Notes on the sheet:
  //   ALU ops
  //   stall logic
  //   Nop logic
  //   conditional branches
  //   branches
  //   Take Branch
  //   Halt Logic
endmodule
