// Digital circuit frontpanel.dig as structural Verilog
module frontpanel (
  input  clock,
  input  erun,
  output [15:0] R0,
  output [15:0] R1,
  output [15:0] R2,
  output [15:0] R3,
  output halt,
  output error,
  output [7:0] PC
);

  wire brindha32_1_p1, brindha32_1_p4, brindha32_1_p13, instrdisplay_1_p1, instrdisplay_1_p2,
       instrdisplay_1_p3, instrdisplay_1_p4, instrdisplay_1_p5, instrdisplay_1_p6, jump, L, or_1_out, R, rd,
       rd_valid, regdisplay_1_p3, regdisplay_1_p6, regdisplay_2_p1, regdisplay_2_p2, rs_valid, step_2_out,
       step_out, undriven;
  wire [1:0] rs;
  wire [2:0] cond;
  wire [4:0] op;
  wire [7:0] brindha32_1_p2;
  wire [13:0] brindha32_1_p6;
  wire [15:0] blockramdualport_1_d, blockramdualport_2_d, brindha32_1_p5, instrdisplay_1_d1,
       instrdisplay_1_d2, instrdisplay_1_d3, instrdisplay_1_d4, instrdisplay_1_d5, instrdisplay_1_d6,
       regdisplay_1_p1, regdisplay_1_p4, regdisplay_2_d1, regdisplay_2_d2;

  SixteenSeg sixteenseg_1 (.led(regdisplay_1_p1), .dp(regdisplay_1_p3));
  SixteenSeg sixteenseg_2 (.led(regdisplay_1_p4), .dp(regdisplay_1_p6));
  // regdisplay regdisplay_1: pin names not known; wires that end beside it: regdisplay_1_p1, 1'b1, regdisplay_1_p3, regdisplay_1_p4, jump, regdisplay_1_p6, rd
  Seven_Seg_Hex seven_seg_hex_1 ();  // open: d, dp
  // hexdisplay hexdisplay_1: pin names not known; wires that end beside it: rd_valid, L
  Seven_Seg_Hex seven_seg_hex_2 ();  // open: d, dp
  Seven_Seg_Hex seven_seg_hex_3 ();  // open: d, dp
  Seven_Seg_Hex seven_seg_hex_4 ();  // open: d, dp
  BlockRAMDualPort #(.AddrBits(8), .isProgramMemory("true"), .Bits(16)) blockramdualport_1 (
    .A(brindha32_1_p2), .Din({16{1'b0}}), .str(1'b0), .C(brindha32_1_p1), .D(blockramdualport_1_d));
  BlockRAMDualPort #(.AddrBits(14), .Bits(16)) blockramdualport_2 (
    .A(brindha32_1_p6), .Din(brindha32_1_p5), .str(brindha32_1_p4), .C(brindha32_1_p1),
    .D(blockramdualport_2_d));
  SixteenSeg sixteenseg_3 (.led(instrdisplay_1_d1), .dp(instrdisplay_1_p1));
  SixteenSeg sixteenseg_4 (.led(instrdisplay_1_d2), .dp(instrdisplay_1_p2));
  instrdisplay instrdisplay_1 (
    .D1(instrdisplay_1_d1), .P1(instrdisplay_1_p1), .D2(instrdisplay_1_d2), .P2(instrdisplay_1_p2),
    .D3(instrdisplay_1_d3), .P3(instrdisplay_1_p3), .D4(instrdisplay_1_d4), .P4(instrdisplay_1_p4),
    .D5(instrdisplay_1_d5), .P5(instrdisplay_1_p5), .D6(instrdisplay_1_d6), .P6(instrdisplay_1_p6), .l(op),
    .C(cond));
  Button step (.out(step_out));
  Button step_2 (.out(step_2_out));
  SixteenSeg sixteenseg_5 (.led(instrdisplay_1_d3), .dp(instrdisplay_1_p3));
  SixteenSeg sixteenseg_6 (.led(instrdisplay_1_d4), .dp(instrdisplay_1_p4));
  or or_1 (or_1_out, step_2_out, erun);
  // brindha32 brindha32_1: pin names not known; wires that end beside it: brindha32_1_p1, brindha32_1_p2, blockramdualport_1_d, brindha32_1_p4, brindha32_1_p5, brindha32_1_p6, blockramdualport_2_d, jump, rd_valid, or_1_out, step_out, clock, brindha32_1_p13, PC, R0, R1, R2
  SixteenSeg sixteenseg_7 (.led(instrdisplay_1_d5), .dp(instrdisplay_1_p5));
  SixteenSeg sixteenseg_8 (.led(instrdisplay_1_d6), .dp(instrdisplay_1_p6));
  Seven_Seg_Hex seven_seg_hex_5 ();  // open: d, dp
  Seven_Seg_Hex seven_seg_hex_6 ();  // open: d, dp
  // hexdisplay hexdisplay_2: pin names not known; wires that end beside it: rs_valid, op, cond, L, 1'b1, R, R, rd
  Seven_Seg_Hex seven_seg_hex_7 ();  // open: d, dp
  Seven_Seg_Hex seven_seg_hex_8 ();  // open: d, dp
  LED stalled (.in(brindha32_1_p13));
  LED T (.in(undriven));
  SixteenSeg sixteenseg_9 (.led(regdisplay_2_d1), .dp(regdisplay_2_p1));
  SixteenSeg sixteenseg_10 (.led(regdisplay_2_d2), .dp(regdisplay_2_p2));
  regdisplay regdisplay_2 (
    .D1(regdisplay_2_d1), .P1(regdisplay_2_p1), .D2(regdisplay_2_d2), .P2(regdisplay_2_p2), .E(rs_valid),
    .J(1'b0), .R(rs));

  // Notes on the sheet:
  //   clock: Hz: 10
endmodule
