// Digital circuit hexdisplay.dig as structural Verilog
module hexdisplay (
  input  E,
  input  [15:0] V,
  output [3:0] D5,
  output P5,
  output [3:0] D6,
  output P6,
  output [3:0] D7,
  output P7,
  output [3:0] D8,
  output P8
);

  assign D5 = E ? V[15:12] : 4'bz;  // Driver driver_1
  assign D6 = E ? V[11:8] : 4'bz;  // Driver driver_2
  assign D7 = E ? V[7:4] : 4'bz;  // Driver driver_3
  assign D8 = E ? V[3:0] : 4'bz;  // Driver driver_4

  assign P5 = 1'b0;
  assign P6 = 1'b0;
  assign P7 = 1'b0;
  assign P8 = 1'b0;
endmodule
