// Digital circuit test_suite.dig as structural Verilog
module test_suite (
  input  clock,
  output [3:0] PC,
  output error,
  output halt
);

  // frontpanel frontpanel_1: pin names not known; wires that end beside it: clock, PC, error, halt
endmodule

/* Test case add:
clock error halt

# #include "../cpudef.asm"
#
# move r1, 5
# move r2, 3
# add r1, r2
# add r1, 2
# musteq r1, 10

program(0x051c, 0x032c, 0x0091, 0x0210, 0x0a1a)

let i = 0;
while(!(halt | error | (i >= 100)))
  let i = i + 1;
  0 0 0
  1 x x
end while
0 0 1
*/
